// Digital circuit ALU.dig as structural Verilog
module ALU (
  input  [31:0] x,
  input  [31:0] y,
  input  [2:0] func,
  output [31:0] result,
  output iszero
);

  wire [0:0] comparator_1_lt;
  wire [31:0] add_1_s, and_1_out, or_1_out, sub_1_s;

  Add #(.Bits(32)) add_1 (.a(x), .b(y), .c_i(1'b0), .s(add_1_s));  // open: c_o
  Sub #(.Bits(32)) sub_1 (.a(x), .b(y), .c_i(1'b0), .s(sub_1_s));  // open: c_o
  assign and_1_out = x & y;  // And and_1, 32 bits wide
  assign or_1_out = x | y;  // Or or_1, 32 bits wide
  Comparator #(.Signed("true"), .Bits(32)) comparator_1 (.a(x), .b(y), .lt(comparator_1_lt[0]));  // open: gt, eq
  Multiplexer #(.Selector_Bits(3), .Bits(32)) multiplexer_1 (
    .sel(func), .in_0(add_1_s), .in_1(sub_1_s), .in_2(and_1_out), .in_3(or_1_out),
    .in_4({{31{1'b0}}, comparator_1_lt[0]}), .in_5({32{1'b0}}), .in_6({32{1'b0}}), .in_7({32{1'b0}}),
    .out(result));
  Comparator #(.Bits(32)) comparator_2 (.a(result), .b({32{1'b0}}), .eq(iszero));  // open: gt, lt
endmodule
