// Digital circuit ALU_Control.dig as structural Verilog
module ALU_Control (
  input  [5:0] Func,
  output [2:0] ALUFunc
);

  ROM #(.AddrBits(6), .Bits(3)) AluControl (.A(Func), .sel(1'b1), .D(ALUFunc));

  // Notes on the sheet:
  //   AluControl loads func_signals.hex
endmodule
