// Digital circuit Control_Unit.dig as structural Verilog
module Control_Unit (
  input  [5:0] opc,
  output Jump,
  output Branch,
  output MemRead,
  output MemWrite,
  output [1:0] MemToReg,
  output ALUSrc,
  output RegWrite,
  output [1:0] RegDst,
  output ALUOp,
  output InvOpcode,
  output [2:0] ALUFunc,
  output Jal,
  output Extend
);

  ROM #(.AddrBits(6), .Bits(17)) ControlUnit (
    .A(opc), .sel(1'b1),
    .D({ALUFunc, InvOpcode, Extend, ALUOp, RegDst, RegWrite, ALUSrc, MemToReg, MemWrite, MemRead, Branch, Jal, Jump}));

  // Notes on the sheet:
  //   ControlUnit loads opc_signals.hex
endmodule
