// Digital circuit Mips32Soc.dig as structural Verilog
module Mips32Soc (
  input  clk,
  input  rst
);

  wire ALUOp, ALUSrc, RegDst, RegWrite;
  wire [2:0] alu_control_1_alufunc, ALUFunc, control_unit_1_p6;
  wire [4:0] multiplexer_2_out, rd, rt;
  wire [5:0] func, opcode;
  wire [25:6] Inst_Mem_d;
  wire [31:0] add_1_s, alu_1_result, multiplexer_1_out, multiplexer_3_out, PC_q, registerfile_1_da,
       registerfile_1_db;

  Multiplexer #(.Bits(32)) multiplexer_1 (.sel(rst), .in_0(add_1_s), .in_1({32{1'b0}}), .out(multiplexer_1_out));
  Register #(.Bits(32)) PC (.D(multiplexer_1_out), .C(clk), .en(1'b1), .Q(PC_q));
  // Control_Unit control_unit_1: pin names not known; wires that end beside it: opcode, ALUSrc, RegWrite, RegDst, ALUOp, control_unit_1_p6
  Add #(.Bits(32)) add_1 (.a(PC_q), .b(32'h4), .c_i(1'b0), .s(add_1_s));  // open: c_o
  ROM #(.AddrBits(8), .Bits(32)) Inst_Mem (
    .A(PC_q[9:2]), .sel(1'b1), .D({opcode, Inst_Mem_d[25:21], rt, rd, Inst_Mem_d[10:6], func}));
  Multiplexer #(.Bits(5)) multiplexer_2 (.sel(RegDst), .in_0(rt), .in_1(rd), .out(multiplexer_2_out));
  ALU_Control alu_control_1 (.Func(func), .ALUFunc(alu_control_1_alufunc));
  RegisterFile #(.AddrBits(5), .Bits(32)) registerfile_1 (
    .Din(alu_1_result), .we(RegWrite), .Rw(multiplexer_2_out), .C(clk), .Ra(Inst_Mem_d[25:21]), .Rb(rt),
    .Da(registerfile_1_da), .Db(registerfile_1_db));
  Multiplexer #(.Bits(32)) multiplexer_3 (
    .sel(ALUSrc), .in_0(registerfile_1_db), .in_1({{16{1'b0}}, rd, Inst_Mem_d[10:6], func}),
    .out(multiplexer_3_out));
  Multiplexer #(.Bits(3)) multiplexer_4 (
    .sel(ALUOp), .in_0(control_unit_1_p6), .in_1(alu_control_1_alufunc), .out(ALUFunc));
  ALU alu_1 (.x(registerfile_1_da), .y(multiplexer_3_out), .func(ALUFunc), .result(alu_1_result));  // open: iszero

  // Notes on the sheet:
  //   contents of Inst_Mem (hex, n*v repeats v):
  //   34090064,340a00c8,12a2020,12a2822,3409beef,340af00f,12a4024,12a4025,34090064,340a00c8,
  //   12a582a
endmodule
